# Fritzing sketch PenyiramanTanaman Backup (saved by Fritzing 0.9.3b)
circuit board: 8.46667cm x 5.64444cm

parts:
  U1 = NodeMCU V3.0
  Part2 = Adafruit ADS1115 16Bit I2C ADC [part_number="Adafruit #1085"]
  Part3 = LCD1602-I2C
  Part4 = FC-28 Soil Hygrometer Module
  Part5 = FC-28 Soil Hygrometer Module
  Part6 = FC-28 Soil Hygrometer Module - Probe
  Part7 = FC-28 Soil Hygrometer Module - Probe
  DHT1 = DHT11 Humitidy and Temperature Sensor
  R1 = Resistor [tolerance=±5% resistance=10k package=THT]
  2_Channel_Relay1 = 2 Channel Power Relay
  U2 = LM2596 step down module
  M2 = DC Motor
  M1 = DC Motor
  BATT1 = LiPoly Battery (1300mAh)

nets:
  N1: U1.D1, Part2.SCL, Part3.SCL
  N2: U1.D2, Part2.SDA, Part3.SDA
  N3: U1.D3, DHT1.DATA, R1.Pin_0
  N4: U1.D5, 2_Channel_Relay1.IN1
  VCC: U1.Vin, Part2.VDD, Part3.VCC, Part4.VCC, Part5.VCC, DHT1.VDD, R1.Pin_1, 2_Channel_Relay1.VCC, U2.OUT+
  N5: U1.S3, 2_Channel_Relay1.IN2
  GND: U1.GND, Part2.GND, Part3.GND, Part4.GND, Part5.GND, DHT1.GND, 2_Channel_Relay1.GND, 2_Channel_Relay1.K1-NO, 2_Channel_Relay1.K2-NO, U2.IN-, U2.OUT-, BATT1.negative
  N6: Part2.AIN1, Part5.AO
  N7: Part2.AIN0, Part4.AO
  N8: Part4.POS, Part6.POS
  N9: Part4.NEG, Part6.NEG
  N10: Part5.POS, Part7.POS
  N11: Part5.NEG, Part7.NEG
  N12: 2_Channel_Relay1.K1-NC, M1.pin_1
  N13: 2_Channel_Relay1.K2-NC, M2.pin_1
  N14: U2.IN+, M2.pin_2, M1.pin_2, BATT1.positive

custom parts:
  NodeMCU V3.0: ESP8266 based NodeMCU
  Adafruit ADS1115 16Bit I2C ADC: For microcontrollers without an analog-to-digital converter or when you want a higher-precision ADC, the ADS1115 provides 16-bit precision at 860 samples/second over I2C. The chip can be configured as 4 single-ended input channels, or two differential channels. As a nice bonus, it even includes a programmable gain amplifier, up to x16, to help boost up smaller single/differential signals to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
  LCD1602-I2C: A standard character display, usually with 2x16 characters. Comes in many colors with LCM1602 IIC attached.
  FC-28 Soil Hygrometer Module: The FC-28 is a soil hygrometer module that uses the Texas Instruments LM393 comparator chip to provide an analog measurement of soil humidity. The digital output is high when soil moisture is over a certain threshold, as determined by adjusting the potentiometer.
  FC-28 Soil Hygrometer Module - Probe: The FC-28 is a soil hygrometer module that uses the Texas Instruments LM393 comparator chip to provide an analog measurement of soil humidity.
  DHT11 Humitidy and Temperature Sensor: DHT11 Humidity and Temperature Sensor
  2 Channel Power Relay: A 2 channel power relay. The module operates at 5V.
  LM2596 step down module: LM2596 DC-DC step down power supply module 3 A.
  LiPoly Battery (1300mAh): Lithium Ion Polymer Battery (1300mAh)
